# Fritzing sketch circuit_mega (saved by Fritzing 0.9.3b)

parts:
  RTC = ZS-042 RTC Module
  Joystick = Thumb Joystick
  3_3V_Converter = RioRand LM2596
  5V_Converter = RioRand LM2596
  12V_Power = Battery block 9V
  HM-10 = Bluetooth HC-05 Macho
  DISPLAY_SPI = female pin header, 4 pins [form="♀ (female)"]  # not connected
  I2C = female pin header, 2 pins [form="♀ (female)"]  # not connected
  SD_CARD = SparkFun - microSD Transflash
  TDS_Analog = female pin header, 1 pin [form="♀ (female)"]  # not connected
  NeoPixel = female pin header, 1 pin [form="♀ (female)"]  # not connected
  MotorDriver = female pin header, 3 pins [form="♀ (female)"]  # not connected
  Arduino_MEGA = Arduino Mega 2560 (Rev3)

nets:
  GND: RTC.GND, Joystick.GND, 5V_Converter.Pin_4, HM-10.GND, SD_CARD.GND, Arduino_MEGA.GND
  VCC: RTC.VCC, Joystick.VCC, 5V_Converter.Pin_3, HM-10.VCC, SD_CARD.VCC, Arduino_MEGA.5V
  N1: 3_3V_Converter.Pin_1, 5V_Converter.Pin_1, 12V_Power.+
  N2: 3_3V_Converter.Pin_2, 5V_Converter.Pin_2, 12V_Power.-

notes:
  5V Conveter
  3.3V Conveter
  MISO
  MOSI
  SCLK
  CS
  SDA
  SCL
  HM-10 BLE
  SD Module
  RTC
  Joystick
  Arduino MEGA
  DISPLAY SPI
  TDS Analog
  GND
  5V
  Data
  NeoPixel
  EN1
  IN1/2
  IN2/1
  MotorDriver
